// Logisim project calculator.circ as structural Verilog: 10 circuits, main circuit final
module BCD (
  input  [3:0] in_1,
  output [3:0] out_2
);

  wire and_1_out, and_2_out, bitselector_1_out, bitselector_2_out, bitselector_3_out, or_1_out;

  BitSelector #(.width(4)) bitselector_1 (.in(in_1), .out(bitselector_1_out), .sel(2'b11));
  BitSelector #(.width(4)) bitselector_2 (.in(in_1), .out(bitselector_2_out), .sel(2'b10));
  BitSelector #(.width(4)) bitselector_3 (.in(in_1), .out(bitselector_3_out), .sel(2'b01));
  and and_1 (and_1_out, bitselector_1_out, bitselector_3_out);
  and and_2 (and_2_out, bitselector_1_out, bitselector_2_out);
  or or_1 (or_1_out, and_1_out, and_2_out);
  assign out_2 = {{3{or_1_out}}, or_1_out};  // Bit_Extender bit_extender_1
endmodule

module somabcd (
  input  in_1,
  input  [3:0] in_2,
  output [3:0] out_3,
  output out_4
);

  wire [3:0] and_1_out, bcd_1_out_2;

  BCD bcd_1 (.in_1(in_2), .out_2(bcd_1_out_2));
  assign and_1_out = bcd_1_out_2 & 4'b0110;  // AND_Gate and_1, 4 bits wide
  Adder #(.width(4)) adder_1 (.a(and_1_out), .b(in_2), .out(out_3), .cin(in_1), .cout(out_4));
endmodule

module display2 (
  input  [3:0] in_1,
  input  [3:0] in_2,
  input  [3:0] in_3,
  input  [3:0] in_4,
  output out_5,
  output out_6,
  output out_7,
  output out_8,
  output out_9,
  output out_10,
  output out_11,
  output out_12,
  output out_13,
  output out_14,
  output out_15,
  output out_16,
  output out_17,
  output out_18,
  output out_19,
  output out_20,
  output out_21,
  output out_22,
  output out_23,
  output out_24,
  output out_25,
  output out_26,
  output out_27,
  output out_28,
  output out_29,
  output out_30,
  output out_31,
  output out_32
);

  // _7_segment_display_driver 7_segment_display_driver_1: pin names not known; wires that end beside it: in_1[3], in_1[2], in_1[1], in_1[0], out_5, out_6, out_7, out_8, out_9, out_10, out_11
  // _7_segment_display_driver 7_segment_display_driver_2: pin names not known; wires that end beside it: in_2[3], in_2[2], in_2[1], in_2[0], out_12, out_13, out_14, out_15, out_16, out_17, out_18
  // _7_segment_display_driver 7_segment_display_driver_3: pin names not known; wires that end beside it: in_3[3], in_3[2], in_3[1], in_3[0], out_19, out_20, out_21, out_22, out_23, out_24, out_25
  // _7_segment_display_driver 7_segment_display_driver_4: pin names not known; wires that end beside it: in_4[3], in_4[2], in_4[1], in_4[0], out_26, out_27, out_28, out_29, out_30, out_31, out_32
endmodule

module teclado2_0 (
  input  [3:0] in_1,
  input  in_2,
  input  in_3,
  output [3:0] out_4,
  output [3:0] out_5,
  output [3:0] out_6,
  output [3:0] out_7
);

  Register #(.width(4)) register_1 (.D(in_1), .Q(out_4), .clk(in_2), .clr(in_3));  // open: en
  Register #(.width(4)) register_2 (.D(out_4), .Q(out_5), .clk(in_2), .clr(in_3));  // open: en
  Register #(.width(4)) register_3 (.D(out_5), .Q(out_6), .clk(in_2), .clr(in_3));  // open: en
  Register #(.width(4)) register_4 (.D(out_6), .Q(out_7), .clk(in_2), .clr(in_3));  // open: en
endmodule

module mult (
  input  [3:0] in_1,
  input  [3:0] in_2,
  input  [3:0] in_3,
  input  [3:0] in_4,
  output [15:0] out_5
);

  wire adder_1_cout, adder_2_cout;
  wire [15:0] adder_1_out, adder_2_out, bit_extender_1_out, bit_extender_2_out, bit_extender_3_out,
       bit_extender_4_out, multiplier_1_out, multiplier_2_out, multiplier_3_out, multiplier_4_out,
       multiplier_5_out, multiplier_6_out;

  assign bit_extender_1_out = {{12{1'b0}}, in_2};  // Bit_Extender bit_extender_1
  assign bit_extender_2_out = {{12{1'b0}}, in_1};  // Bit_Extender bit_extender_2
  assign bit_extender_3_out = {{12{1'b0}}, in_3};  // Bit_Extender bit_extender_3
  assign bit_extender_4_out = {{12{1'b0}}, in_4};  // Bit_Extender bit_extender_4
  Multiplier #(.width(16)) multiplier_1 (.a(bit_extender_3_out), .b(16'ha), .out(multiplier_1_out));  // open: cin, cout
  Multiplier #(.width(16)) multiplier_2 (.a(bit_extender_1_out), .b(16'ha), .out(multiplier_2_out));  // open: cin, cout
  Multiplier #(.width(16)) multiplier_3 (.a(bit_extender_2_out), .b(16'ha), .out(multiplier_3_out));  // open: cin, cout
  Adder #(.width(16)) adder_1 (
    .a(bit_extender_4_out), .b(multiplier_1_out), .out(adder_1_out), .cout(adder_1_cout));  // open: cin
  Multiplier #(.width(16)) multiplier_4 (.a(multiplier_2_out), .b(16'ha), .out(multiplier_4_out));  // open: cin, cout
  Multiplier #(.width(16)) multiplier_5 (.a(multiplier_3_out), .b(16'ha), .out(multiplier_5_out));  // open: cin, cout
  Multiplier #(.width(16)) multiplier_6 (.a(multiplier_5_out), .b(16'ha), .out(multiplier_6_out));  // open: cin, cout
  Adder #(.width(16)) adder_2 (
    .a(adder_1_out), .b(multiplier_4_out), .out(adder_2_out), .cin(adder_1_cout), .cout(adder_2_cout));
  Adder #(.width(16)) adder_3 (.a(adder_2_out), .b(multiplier_6_out), .out(out_5), .cin(adder_2_cout));  // open: cout
endmodule

module jaaj (
  input  in_1,
  input  [15:0] in_2,
  output [15:0] out_3
);

  wire [15:0] and_1_out, and_2_out, and_3_out, bit_extender_1_out, not_1_out, not_2_out, or_1_out;

  assign bit_extender_1_out = {{15{in_1}}, in_1};  // Bit_Extender bit_extender_1
  assign not_1_out = ~in_2;  // NOT_Gate not_1, 16 bits wide
  assign not_2_out = ~bit_extender_1_out;  // NOT_Gate not_2, 16 bits wide
  assign and_1_out = 16'h1 & bit_extender_1_out;  // AND_Gate and_1, 16 bits wide
  assign and_2_out = bit_extender_1_out & not_1_out;  // AND_Gate and_2, 16 bits wide
  assign and_3_out = not_2_out & in_2;  // AND_Gate and_3, 16 bits wide
  assign or_1_out = and_2_out | and_3_out;  // OR_Gate or_1, 16 bits wide
  Adder #(.width(16)) adder_1 (.a(and_1_out), .b(or_1_out), .out(out_3));  // open: cin, cout
endmodule

module caso2 (
  input  [3:0] in_1,
  input  [3:0] in_2,
  output [3:0] out_3
);

  wire and_1_out, and_2_out, and_3_out, not_1_out, not_2_out, not_3_out, not_4_out, not_5_out, not_6_out,
       not_7_out, not_8_out, not_9_out, not_10_out, or_1_out;
  wire [3:0] bit_extender_1_out;

  not not_1 (not_1_out, in_1[3]);
  not not_2 (not_2_out, in_2[2]);
  not not_3 (not_3_out, in_2[1]);
  not not_4 (not_4_out, in_1[1]);
  not not_5 (not_5_out, in_1[2]);
  not not_6 (not_6_out, in_2[2]);
  not not_7 (not_7_out, in_2[1]);
  not not_8 (not_8_out, in_1[1]);
  not not_9 (not_9_out, in_1[2]);
  not not_10 (not_10_out, in_2[3]);
  and and_1 (and_1_out, not_1_out, in_1[1], in_1[2], in_1[0], in_2[3], not_2_out, not_3_out, in_2[0]);
  and and_2 (and_2_out, in_1[3], not_4_out, not_5_out, in_2[3], not_6_out, not_7_out);
  and and_3 (and_3_out, in_1[3], not_8_out, not_9_out, in_1[0], not_10_out, in_2[2], in_2[1], in_2[0]);
  or or_1 (or_1_out, and_1_out, and_2_out, and_3_out);
  assign bit_extender_1_out = {{3{or_1_out}}, or_1_out};  // Bit_Extender bit_extender_1
  assign out_3 = bit_extender_1_out & 4'b0110;  // AND_Gate and_4, 4 bits wide
endmodule

module bcdtobin (
  input  [3:0] in_1,
  input  [3:0] in_2,
  input  [3:0] in_3,
  input  [3:0] in_4,
  output [15:0] out_5
);

  wire adder_1_cout, adder_2_cout;
  wire [15:0] adder_1_out, adder_2_out, bit_extender_1_out, bit_extender_2_out, bit_extender_3_out,
       bit_extender_4_out, multiplier_1_out, multiplier_2_out, multiplier_3_out, multiplier_4_out,
       multiplier_5_out, multiplier_6_out;

  assign bit_extender_1_out = {{12{1'b0}}, in_2};  // Bit_Extender bit_extender_1
  assign bit_extender_2_out = {{12{1'b0}}, in_1};  // Bit_Extender bit_extender_2
  assign bit_extender_3_out = {{12{1'b0}}, in_3};  // Bit_Extender bit_extender_3
  assign bit_extender_4_out = {{12{1'b0}}, in_4};  // Bit_Extender bit_extender_4
  Multiplier #(.width(16)) multiplier_1 (.a(bit_extender_3_out), .b(16'ha), .out(multiplier_1_out));  // open: cin, cout
  Multiplier #(.width(16)) multiplier_2 (.a(bit_extender_1_out), .b(16'ha), .out(multiplier_2_out));  // open: cin, cout
  Multiplier #(.width(16)) multiplier_3 (.a(bit_extender_2_out), .b(16'ha), .out(multiplier_3_out));  // open: cin, cout
  Adder #(.width(16)) adder_1 (
    .a(bit_extender_4_out), .b(multiplier_1_out), .out(adder_1_out), .cout(adder_1_cout));  // open: cin
  Multiplier #(.width(16)) multiplier_4 (.a(multiplier_2_out), .b(16'ha), .out(multiplier_4_out));  // open: cin, cout
  Multiplier #(.width(16)) multiplier_5 (.a(multiplier_3_out), .b(16'ha), .out(multiplier_5_out));  // open: cin, cout
  Multiplier #(.width(16)) multiplier_6 (.a(multiplier_5_out), .b(16'ha), .out(multiplier_6_out));  // open: cin, cout
  Adder #(.width(16)) adder_2 (
    .a(adder_1_out), .b(multiplier_4_out), .out(adder_2_out), .cin(adder_1_cout), .cout(adder_2_cout));
  Adder #(.width(16)) adder_3 (.a(adder_2_out), .b(multiplier_6_out), .out(out_5), .cin(adder_2_cout));  // open: cout
endmodule

module bintobcd (
  input  [15:0] in_1,
  output [3:0] out_2,
  output [3:0] out_3,
  output [3:0] out_4,
  output [3:0] out_5
);

  wire [15:0] divider_1_out, divider_2_out;
  wire [15:4] divider_1_rem, divider_2_rem, divider_3_out, divider_3_rem;

  Divider #(.width(16)) divider_1 (
    .a(in_1), .b(16'ha), .out(divider_1_out), .rem({divider_1_rem, out_2}));  // open: upper
  Divider #(.width(16)) divider_2 (
    .a(divider_1_out), .b(16'ha), .out(divider_2_out), .rem({divider_2_rem, out_3}));  // open: upper
  Divider #(.width(16)) divider_3 (
    .a(divider_2_out), .b(16'ha), .out({divider_3_out, out_5}), .rem({divider_3_rem, out_4}));  // open: upper
endmodule

module \final  (
);

  wire _0, _1, _2, _3, _4, _5, _6, _7, _8, _9, a, a1, a2, a3, a4, adder_1_cout, adder_2_cout, adder_3_cout,
       b1, b2, b3, b4, c, c1, c2, c3, c4, d, d1, d2, d3, d4, den, e1, e2, e3, e4, f1, f2, f3, f4, g1, g2, g3,
       g4, i, ia, id, im, is, pri2, register_22_q, register_23_q, register_24_q, register_25_q, ren, s,
       signal, signal2, somabcd_1_out_4, somabcd_2_out_4, somabcd_3_out_4, somabcd_5_out_4, somabcd_6_out_4,
       somabcd_7_out_4, somabcd_8_out_4, somabcd_9_out_4, somabcd_10_out_4, somabcd_11_out_4,
       somabcd_12_out_4, somabcd_13_out_4, subtractor_1_bout, x;
  wire [3:0] adder_9_out, adder_10_out, adder_11_out, adder_12_out, bintobcd_1_out_2, bintobcd_1_out_3,
       bintobcd_1_out_4, bintobcd_1_out_5, bintobcd_2_out_2, bintobcd_2_out_3, bintobcd_2_out_4,
       bintobcd_2_out_5, bintobcd_3_out_2, bintobcd_3_out_3, bintobcd_3_out_4, bintobcd_3_out_5,
       caso2_1_out_3, caso2_2_out_3, caso2_3_out_3, caso2_4_out_3, div1, div2, div3, div4, j1, j2, j3, j4,
       l1, l2, l3, l4, m1, m2, m3, m4, or_3_out, or_4_out, or_5_out, or_6_out, pri1, somabcd_1_out_3,
       somabcd_2_out_3, somabcd_3_out_3, somabcd_4_out_3, somabcd_5_out_3, somabcd_6_out_3, somabcd_7_out_3,
       somabcd_8_out_3, somabcd_9_out_3, somabcd_10_out_3, somabcd_11_out_3, somabcd_12_out_3,
       somabcd_13_out_3, somabcd_14_out_3, somabcd_15_out_3, somabcd_16_out_3, sub1, sub2, sub3, sub4, sum1,
       sum2, sum3, sum4, t1, t2, t3, t4, u1, u2, u3, u4;
  wire [15:0] bin1, bin2, divider_1_out, jaaj_1_out_3, multiplier_1_out, subtractor_1_out;

  _7_Segment_Display u_7_segment_display_1 (.g(signal2));  // open: f, a, b, e, d, c, dp
  somabcd somabcd_1 (.in_2(l1), .out_4(somabcd_1_out_4), .out_3(somabcd_1_out_3));  // open: in_1
  somabcd somabcd_2 (.in_2(l2), .in_1(somabcd_1_out_4), .out_4(somabcd_2_out_4), .out_3(somabcd_2_out_3));
  somabcd somabcd_3 (.in_2(l3), .in_1(somabcd_2_out_4), .out_4(somabcd_3_out_4), .out_3(somabcd_3_out_3));
  somabcd somabcd_4 (.in_2(l4), .in_1(somabcd_3_out_4), .out_3(somabcd_4_out_3));  // open: out_4
  _7_Segment_Display u_7_segment_display_2 (.g(g4), .f(f4), .a(a4), .b(b4), .e(e4), .d(d4), .c(c4));  // open: dp
  _7_Segment_Display u_7_segment_display_3 (.g(g3), .f(f3), .a(a3), .b(b3), .e(e3), .d(d3), .c(c3));  // open: dp
  Button u__7 (.out(_7));
  Button u__8 (.out(_8));
  Button u__5 (.out(_5));
  Button u__4 (.out(_4));
  Button u__2 (.out(_2));
  Button u__1 (.out(_1));
  Button u__0 (.out(_0));
  Button u_C (.out(c));
  somabcd somabcd_5 (.in_2(somabcd_6_out_3), .out_4(somabcd_5_out_4), .out_3(somabcd_5_out_3));  // open: in_1
  somabcd somabcd_6 (.in_2(somabcd_1_out_3), .out_4(somabcd_6_out_4), .out_3(somabcd_6_out_3));  // open: in_1
  somabcd somabcd_7 (.in_2(somabcd_5_out_3), .out_4(somabcd_7_out_4), .out_3(somabcd_7_out_3));  // open: in_1
  somabcd somabcd_8 (.in_2(somabcd_10_out_3), .in_1(somabcd_5_out_4), .out_4(somabcd_8_out_4), .out_3(somabcd_8_out_3));
  somabcd somabcd_9 (.in_2(somabcd_8_out_3), .in_1(somabcd_7_out_4), .out_4(somabcd_9_out_4), .out_3(somabcd_9_out_3));
  somabcd somabcd_10 (
    .in_2(somabcd_2_out_3), .in_1(somabcd_6_out_4), .out_4(somabcd_10_out_4), .out_3(somabcd_10_out_3));
  somabcd somabcd_11 (
    .in_2(somabcd_3_out_3), .in_1(somabcd_10_out_4), .out_4(somabcd_11_out_4), .out_3(somabcd_11_out_3));
  somabcd somabcd_12 (
    .in_2(somabcd_11_out_3), .in_1(somabcd_8_out_4), .out_4(somabcd_12_out_4), .out_3(somabcd_12_out_3));
  somabcd somabcd_13 (
    .in_2(somabcd_12_out_3), .in_1(somabcd_9_out_4), .out_4(somabcd_13_out_4), .out_3(somabcd_13_out_3));
  somabcd somabcd_14 (.in_2(somabcd_4_out_3), .in_1(somabcd_11_out_4), .out_3(somabcd_14_out_3));  // open: out_4
  somabcd somabcd_15 (.in_2(somabcd_16_out_3), .in_1(somabcd_13_out_4), .out_3(somabcd_15_out_3));  // open: out_4
  somabcd somabcd_16 (.in_2(somabcd_14_out_3), .in_1(somabcd_12_out_4), .out_3(somabcd_16_out_3));  // open: out_4
  Adder #(.width(4)) adder_1 (.a(u1), .b(t1), .out(j1), .cout(adder_1_cout));  // open: cin
  Adder #(.width(4)) adder_2 (.a(u2), .b(t2), .out(j2), .cin(adder_1_cout), .cout(adder_2_cout));
  Adder #(.width(4)) adder_3 (.a(u3), .b(t3), .out(j3), .cin(adder_2_cout), .cout(adder_3_cout));
  Adder #(.width(4)) adder_4 (.a(u4), .b(t4), .out(j4), .cin(adder_3_cout));  // open: cout
  _7_Segment_Display u_7_segment_display_4 (.g(g1), .f(f1), .a(a1), .b(b1), .e(e1), .d(d1), .c(c1));  // open: dp
  _7_Segment_Display u_7_segment_display_5 (.g(g2), .f(f2), .a(a2), .b(b2), .e(e2), .d(d2), .c(c2));  // open: dp
  Button u__9 (.out(_9));
  Button u__6 (.out(_6));
  Button u__3 (.out(_3));
  Button button (.out(i));
  Register #(.width(4)) register_1 (.D(t4), .Q(u4), .clk(ren), .clr(c));  // open: en
  Register #(.width(4)) register_2 (.D(somabcd_7_out_3), .Q(sum1), .clk(ia), .clr(c));  // open: en
  Register #(.width(4)) register_3 (.D(somabcd_9_out_3), .Q(sum2), .clk(ia), .clr(c));  // open: en
  Register #(.width(4)) register_4 (.D(somabcd_13_out_3), .Q(sum3), .clk(ia), .clr(c));  // open: en
  Register #(.width(4)) register_5 (.D(somabcd_15_out_3), .Q(sum4), .clk(ia), .clr(c));  // open: en
  Subtractor #(.width(16)) subtractor_1 (
    .a(bin1), .b(bin2), .out(subtractor_1_out), .bout(subtractor_1_bout));  // open: bin
  Button button_2 (.out(s));
  Button button_3 (.out(d));
  Button u_x (.out(x));
  Button button_4 (.out(a));
  Register #(.width(4)) register_6 (.D(t3), .Q(u3), .clk(ren), .clr(c));  // open: en
  Register #(.width(1)) register_7 (.D(subtractor_1_bout), .Q(signal), .clk(i), .clr(c));  // open: en
  Multiplier #(.width(16)) multiplier_1 (.a(bin1), .b(bin2), .out(multiplier_1_out));  // open: cin, cout
  jaaj jaaj_1 (.in_1(subtractor_1_bout), .in_2(subtractor_1_out), .out_3(jaaj_1_out_3));
  Register #(.width(4)) register_8 (.D(t2), .Q(u2), .clk(ren), .clr(c));  // open: en
  bintobcd bintobcd_1 (
    .in_1(multiplier_1_out), .out_2(bintobcd_1_out_2), .out_3(bintobcd_1_out_3), .out_4(bintobcd_1_out_4),
    .out_5(bintobcd_1_out_5));
  bintobcd bintobcd_2 (
    .in_1(jaaj_1_out_3), .out_2(bintobcd_2_out_2), .out_3(bintobcd_2_out_3), .out_4(bintobcd_2_out_4),
    .out_5(bintobcd_2_out_5));
  Register #(.width(4)) register_9 (.D(t1), .Q(u1), .clk(ren), .clr(c));  // open: en
  Register #(.width(4)) register_10 (.D(bintobcd_1_out_2), .Q(m1), .clk(im), .clr(c));  // open: en
  Register #(.width(4)) register_11 (.D(bintobcd_1_out_3), .Q(m2), .clk(im), .clr(c));  // open: en
  Register #(.width(4)) register_12 (.D(bintobcd_1_out_4), .Q(m3), .clk(im), .clr(c));  // open: en
  Register #(.width(4)) register_13 (.D(bintobcd_1_out_5), .Q(m4), .clk(im), .clr(c));  // open: en
  Register #(.width(4)) register_14 (.D(bintobcd_2_out_2), .Q(sub1), .clk(is), .clr(c));  // open: en
  Register #(.width(4)) register_15 (.D(bintobcd_2_out_3), .Q(sub2), .clk(is), .clr(c));  // open: en
  Register #(.width(4)) register_16 (.D(bintobcd_2_out_4), .Q(sub3), .clk(is), .clr(c));  // open: en
  Register #(.width(4)) register_17 (.D(bintobcd_2_out_5), .Q(sub4), .clk(is), .clr(c));  // open: en
  Divider #(.width(16)) divider_1 (.a(bin1), .b(bin2), .out(divider_1_out));  // open: upper, rem
  bcdtobin bcdtobin_1 (.in_1(u4), .in_2(u3), .in_3(u2), .in_4(u1), .out_5(bin1));
  caso2 caso2_1 (.in_1(t1), .in_2(u1), .out_3(caso2_1_out_3));
  caso2 caso2_2 (.in_1(t2), .in_2(u2), .out_3(caso2_2_out_3));
  caso2 caso2_3 (.in_1(t3), .in_2(u3), .out_3(caso2_3_out_3));
  caso2 caso2_4 (.in_1(t4), .in_2(u4), .out_3(caso2_4_out_3));
  bintobcd bintobcd_3 (
    .in_1(divider_1_out), .out_2(bintobcd_3_out_2), .out_3(bintobcd_3_out_3), .out_4(bintobcd_3_out_4),
    .out_5(bintobcd_3_out_5));
  bcdtobin bcdtobin_2 (.in_1(t4), .in_2(t3), .in_3(t2), .in_4(t1), .out_5(bin2));
  or or_1 (ren, x, a, d, s);
  Priority_Encoder #(.select(4), .disabled(0)) priority_encoder_1 (
    .in0(_0), .in1(_1), .in2(_2), .in3(_3), .in4(_4), .in5(_5), .in6(_6), .in7(_7), .in8(_8), .in9(_9),
    .out(pri1), .gs(pri2));  // open: in10, in11, in12, in13, in14, in15, en_out, en_in
  Adder #(.width(4)) adder_5 (.a(caso2_1_out_3), .b(j1), .out(l1));  // open: cin, cout
  Adder #(.width(4)) adder_6 (.a(caso2_2_out_3), .b(j2), .out(l2));  // open: cin, cout
  Adder #(.width(4)) adder_7 (.a(caso2_3_out_3), .b(j3), .out(l3));  // open: cin, cout
  Adder #(.width(4)) adder_8 (.a(caso2_4_out_3), .b(j4), .out(l4));  // open: cin, cout
  Register #(.width(4)) register_18 (.D(bintobcd_3_out_2), .Q(div1), .clk(id), .clr(c));  // open: en
  Register #(.width(4)) register_19 (.D(bintobcd_3_out_3), .Q(div2), .clk(id), .clr(c));  // open: en
  Register #(.width(4)) register_20 (.D(bintobcd_3_out_4), .Q(div3), .clk(id), .clr(c));  // open: en
  Register #(.width(4)) register_21 (.D(bintobcd_3_out_5), .Q(div4), .clk(id), .clr(c));  // open: en
  Register #(.width(1), .trigger("falling")) register_22 (.D(1'b1), .Q(register_22_q), .clk(a), .clr(c));  // open: en
  Register #(.width(1), .trigger("falling")) register_23 (.D(1'b1), .Q(register_23_q), .clk(s), .clr(c));  // open: en
  Register #(.width(1), .trigger("falling")) register_24 (.D(1'b1), .Q(register_24_q), .clk(d), .clr(c));  // open: en
  Register #(.width(1), .trigger("falling")) register_25 (.D(1'b1), .Q(register_25_q), .clk(x), .clr(c));  // open: en
  or or_2 (den, x, s, d, a, i, c);
  and and_1 (ia, register_22_q, i);
  and and_2 (is, register_23_q, i);
  and and_3 (id, register_24_q, i);
  and and_4 (im, register_25_q, i);
  assign or_3_out = sum1 | div1 | m1 | sub1;  // OR_Gate or_3, 4 bits wide
  assign or_4_out = sum2 | div2 | m2 | sub2;  // OR_Gate or_4, 4 bits wide
  assign or_5_out = sum3 | div3 | m3 | sub3;  // OR_Gate or_5, 4 bits wide
  assign or_6_out = sum4 | div4 | m4 | sub4;  // OR_Gate or_6, 4 bits wide
  teclado2_0 teclado2_0_1 (.in_1(pri1), .in_2(pri2), .in_3(den), .out_4(t1), .out_5(t2), .out_6(t3), .out_7(t4));
  Adder #(.width(4)) adder_9 (.a(t1), .b(or_3_out), .out(adder_9_out));  // open: cin, cout
  display2 display2_1 (
    .in_1(adder_9_out), .in_2(adder_10_out), .in_3(adder_11_out), .in_4(adder_12_out), .out_5(a1),
    .out_6(b1), .out_7(c1), .out_8(d1), .out_9(e1), .out_10(f1), .out_11(g1), .out_12(a2), .out_13(b2),
    .out_14(c2), .out_15(d2), .out_16(e2), .out_17(f2), .out_18(g2), .out_19(a3), .out_20(b3), .out_21(c3),
    .out_22(d3), .out_23(e3), .out_24(f3), .out_25(g3), .out_26(a4), .out_27(b4), .out_28(c4), .out_29(d4),
    .out_30(e4), .out_31(f4), .out_32(g4));
  Adder #(.width(4)) adder_10 (.a(t2), .b(or_4_out), .out(adder_10_out));  // open: cin, cout
  Adder #(.width(4)) adder_11 (.a(t3), .b(or_5_out), .out(adder_11_out));  // open: cin, cout
  Adder #(.width(4)) adder_12 (.a(t4), .b(or_6_out), .out(adder_12_out));  // open: cin, cout
  and and_5 (signal2, signal, register_23_q);

  // Notes on the sheet:
  //   SOMA
  //   SUBTRAÇÂO
  //   REGISTRADORES QUE SALVAM OS NÙMEROS
  //   MULTIPLICAÇÂO
  //   ENTRADA DO DISPLAY
  //   PASSA O NÚMERO PARA O DISPLAY
  //   DIVISÂO
  //   CONVERSORES
  //   RESETA O DISPLAY
  //   DISPLAY
  //   ENABLE DAS OPERAÇÔES
endmodule
